// Logisim project Task2.circ as structural Verilog: 1 circuit, main circuit main
module main (
  input  Cin,
  input  A0,
  input  B0,
  input  A1,
  input  B1,
  input  A2,
  input  B2,
  input  A3,
  input  B3,
  output O0,
  output O1,
  output O2,
  output O3,
  output Cout
);

  wire and_1_out, and_2_out, and_3_out, and_4_out, and_5_out, and_6_out, and_7_out, and_8_out, or_1_out,
       or_2_out, or_3_out, xor_1_out, xor_2_out, xor_3_out, xor_4_out;

  xor xor_1 (xor_1_out, Cin, A0);
  xor xor_2 (xor_2_out, or_1_out, A1);
  xor xor_3 (xor_3_out, or_2_out, A2);
  xor xor_4 (xor_4_out, or_3_out, A3);
  and and_1 (and_1_out, Cin, A0);
  xor xor_5 (O0, xor_1_out, B0);
  and and_2 (and_2_out, xor_1_out, B0);
  xor xor_6 (O1, xor_2_out, B1);
  and and_3 (and_3_out, xor_2_out, B1);
  and and_4 (and_4_out, or_1_out, A1);
  xor xor_7 (O2, xor_3_out, B2);
  and and_5 (and_5_out, xor_3_out, B2);
  and and_6 (and_6_out, or_2_out, A2);
  and and_7 (and_7_out, xor_4_out, B3);
  and and_8 (and_8_out, or_3_out, A3);
  xor xor_8 (O3, xor_4_out, B3);
  or or_1 (or_1_out, and_2_out, and_1_out);
  or or_2 (or_2_out, and_3_out, and_4_out);
  or or_3 (or_3_out, and_5_out, and_6_out);
  or or_4 (Cout, and_7_out, and_8_out);
endmodule
