// Logisim project Task4_updatedCounter.circ as structural Verilog: 1 circuit, main circuit main
module main (
  input  in_1,
  input  in_2,
  input  U,
  output LSB,
  output MSB
);

  wire and_1_out, and_2_out, and_3_out, and_4_out, and_5_out, and_6_out, CLK_out, not_1_out, not_2_out,
       or_1_out, or_2_out, or_3_out, or_4_out;

  not not_1 (not_1_out, LSB);
  Clock CLK (.out(CLK_out));
  not not_2 (not_2_out, MSB);
  or or_1 (or_1_out, not_1_out, U);
  buf and_1 (and_1_out, not_1_out);  // AND_Gate
  D_Flip_Flop Q0 (.D(or_2_out), .clk(CLK_out), .Q(LSB), .reset(in_1));  // open: Qn, preset
  and and_2 (and_2_out, or_1_out, MSB);
  and and_3 (and_3_out, and_1_out, U);
  or or_2 (or_2_out, and_2_out, and_3_out);
  and and_4 (and_4_out, LSB, MSB);
  D_Flip_Flop Q1 (.D(or_3_out), .clk(CLK_out), .Q(MSB), .reset(in_2));  // open: Qn, preset
  and and_5 (and_5_out, MSB, U);
  or or_3 (or_3_out, and_4_out, or_4_out);
  and and_6 (and_6_out, U, LSB);
  or or_4 (or_4_out, and_5_out, and_6_out);
endmodule
