// Logisim project Task3.circ as structural Verilog: 1 circuit, main circuit main
module main (
  input  I3,
  input  I2,
  input  I1,
  input  I0,
  input  EN,
  output Q3,
  output Q1,
  output Q2,
  output Q0
);

  wire CLK_out, d_ff_1_q, d_ff_2_q, d_ff_3_q, d_ff_4_q, multiplexer_1_out, multiplexer_2_out,
       multiplexer_3_out, multiplexer_4_out;

  Multiplexer multiplexer_1 (.in0(d_ff_1_q), .in1(I0), .out(multiplexer_1_out), .sel(EN));
  Clock CLK (.out(CLK_out));
  D_Flip_Flop d_ff_1 (.D(multiplexer_1_out), .clk(CLK_out), .Q(d_ff_1_q), .reset(Q0));  // open: Qn, preset
  D_Flip_Flop d_ff_2 (.D(multiplexer_2_out), .clk(CLK_out), .Q(d_ff_2_q), .reset(Q1));  // open: Qn, preset
  Multiplexer multiplexer_2 (.in0(d_ff_2_q), .in1(I1), .out(multiplexer_2_out), .sel(EN));
  Multiplexer multiplexer_3 (.in0(d_ff_3_q), .in1(I2), .out(multiplexer_3_out), .sel(EN));
  D_Flip_Flop d_ff_3 (.D(multiplexer_3_out), .clk(CLK_out), .Q(d_ff_3_q), .reset(Q2));  // open: Qn, preset
  Multiplexer multiplexer_4 (.in0(d_ff_4_q), .in1(I3), .out(multiplexer_4_out), .sel(EN));
  D_Flip_Flop d_ff_4 (.D(multiplexer_4_out), .clk(CLK_out), .Q(d_ff_4_q), .reset(Q3));  // open: Qn, preset
endmodule
