// Logisim project Task4.circ as structural Verilog: 1 circuit, main circuit main
module main (
  input  I2,
  input  I1,
  output LSB,
  output MSB
);

  wire CLK_out, not_1_out, or_1_out, or_2_out;

  not not_1 (not_1_out, LSB);
  Clock CLK (.out(CLK_out));
  or or_1 (or_1_out, MSB, not_1_out);
  D_Flip_Flop Q0 (.D(or_1_out), .clk(CLK_out), .Q(LSB), .reset(I1));  // open: Qn, preset
  D_Flip_Flop Q1 (.D(or_2_out), .clk(CLK_out), .Q(MSB), .reset(I2));  // open: Qn, preset
  or or_2 (or_2_out, MSB, LSB);
endmodule
